# Fritzing sketch red-phone (saved by Fritzing 0.9.3b)
breadboards: 1

parts:
  Raspberry_Pi_Zero1 = Raspberry Pi Zero
  Q1 = NPN-Transistor [package="TO92 [THT]"]  # not connected
  Q2 = NPN-Transistor [package="TO92 [THT]"]  # not connected
  SP1 = SPEAKER [package=pcb_mount_speaker]

nets:
  N1: Raspberry_Pi_Zero1.GPIO13, SP1.-
  N2: Raspberry_Pi_Zero1.GND, SP1.+
